// Logisim project 2bitSAR.circ as structural Verilog: 1 circuit, main circuit main
module main (
  input  in_1,
  input  in_2,
  output out_3,
  output out_4
);

  wire clock_1_out, d_ff_1_q, d_ff_3_q, d_ff_5_q, d_ff_6_q;

  Clock clock_1 (.out(clock_1_out));
  D_Flip_Flop d_ff_1 (.clk(clock_1_out), .D(1'b0), .Q(d_ff_1_q), .preset(in_1));  // open: Qn, en, reset
  D_Flip_Flop d_ff_2 (.clk(out_4), .D(in_2), .Q(out_3), .preset(d_ff_1_q), .reset(in_1));  // open: Qn, en
  D_Flip_Flop d_ff_3 (.clk(clock_1_out), .D(d_ff_1_q), .Q(d_ff_3_q), .reset(in_1));  // open: Qn, preset, en
  D_Flip_Flop d_ff_4 (.clk(d_ff_6_q), .D(in_2), .Q(out_4), .preset(d_ff_3_q), .reset(in_1));  // open: Qn, en
  D_Flip_Flop d_ff_5 (.clk(clock_1_out), .D(d_ff_3_q), .Q(d_ff_5_q), .reset(in_1));  // open: Qn, preset, en
  D_Flip_Flop d_ff_6 (.clk(1'b0), .D(1'b0), .Q(d_ff_6_q), .preset(d_ff_5_q), .reset(in_1));  // open: Qn, en
endmodule
