// Logisim project 8bitSAR.circ as structural Verilog: 1 circuit, main circuit main
module main (
  input  in_1,
  input  in_2,
  output out_3,
  output out_4,
  output out_5,
  output out_6,
  output out_7,
  output out_8,
  output out_9,
  output out_10
);

  wire clock_1_out, d_ff_1_q, d_ff_3_q, d_ff_5_q, d_ff_7_q, d_ff_9_q, d_ff_11_q, d_ff_13_q, d_ff_15_q,
       d_ff_17_q, d_ff_18_q;

  Clock clock_1 (.out(clock_1_out));
  D_Flip_Flop d_ff_1 (.clk(clock_1_out), .D(1'b0), .Q(d_ff_1_q), .preset(in_1));  // open: Qn, en, reset
  D_Flip_Flop d_ff_2 (.clk(out_6), .D(in_2), .Q(out_5), .preset(d_ff_1_q), .reset(in_1));  // open: Qn, en
  D_Flip_Flop d_ff_3 (.clk(clock_1_out), .D(d_ff_1_q), .Q(d_ff_3_q), .reset(in_1));  // open: Qn, preset, en
  D_Flip_Flop d_ff_4 (.clk(out_7), .D(in_2), .Q(out_6), .preset(d_ff_3_q), .reset(in_1));  // open: Qn, en
  D_Flip_Flop d_ff_5 (.clk(clock_1_out), .D(d_ff_3_q), .Q(d_ff_5_q), .reset(in_1));  // open: Qn, preset, en
  D_Flip_Flop d_ff_6 (.clk(out_9), .D(in_2), .Q(out_7), .preset(d_ff_5_q), .reset(in_1));  // open: Qn, en
  D_Flip_Flop d_ff_7 (.clk(clock_1_out), .D(d_ff_5_q), .Q(d_ff_7_q), .reset(in_1));  // open: Qn, preset, en
  D_Flip_Flop d_ff_8 (.clk(out_10), .D(in_2), .Q(out_9), .preset(d_ff_7_q), .reset(in_1));  // open: Qn, en
  D_Flip_Flop d_ff_9 (.clk(clock_1_out), .D(d_ff_7_q), .Q(d_ff_9_q), .reset(in_1));  // open: Qn, preset, en
  D_Flip_Flop d_ff_10 (.clk(out_8), .D(in_2), .Q(out_10), .preset(d_ff_9_q), .reset(in_1));  // open: Qn, en
  D_Flip_Flop d_ff_11 (.clk(clock_1_out), .D(d_ff_9_q), .Q(d_ff_11_q), .reset(in_1));  // open: Qn, preset, en
  D_Flip_Flop d_ff_12 (.clk(out_3), .D(in_2), .Q(out_8), .preset(d_ff_11_q), .reset(in_1));  // open: Qn, en
  D_Flip_Flop d_ff_13 (.clk(clock_1_out), .D(d_ff_11_q), .Q(d_ff_13_q), .reset(in_1));  // open: Qn, preset, en
  D_Flip_Flop d_ff_14 (.clk(out_4), .D(in_2), .Q(out_3), .preset(d_ff_13_q), .reset(in_1));  // open: Qn, en
  D_Flip_Flop d_ff_15 (.clk(clock_1_out), .D(d_ff_13_q), .Q(d_ff_15_q), .reset(in_1));  // open: Qn, preset, en
  D_Flip_Flop d_ff_16 (.clk(d_ff_18_q), .D(in_2), .Q(out_4), .preset(d_ff_15_q), .reset(in_1));  // open: Qn, en
  D_Flip_Flop d_ff_17 (.clk(clock_1_out), .D(d_ff_15_q), .Q(d_ff_17_q), .reset(in_1));  // open: Qn, preset, en
  D_Flip_Flop d_ff_18 (.clk(1'b0), .D(1'b0), .Q(d_ff_18_q), .preset(d_ff_17_q), .reset(in_1));  // open: Qn, en
endmodule
